// Logisim project micro.circ as structural Verilog: 1 circuit, main circuit EV20_Superescalar
module EV20_Superescalar (
  input  in_1
);

  wire ALU_is_done, ALU_is_free, ALUALULAU_cyout, and_1_out, and_2_out, and_3_out, and_4_out, and_5_out,
       bloque1_1_preload, CLK, CLK2, CLK3, CLK4, CYin, dipswitch_1_sw1, HOLD, MEM_is_done, mem_is_free,
       not_1_out, not_2_out, not_3_out, not_4_out, or_1_out, or_2_out, or_3_out,
       pipeline_register_viewer_1_c_is_enabled, pipeline_register_viewer_2_c_is_enabled,
       pipeline_register_viewer_3_a_is_enabled, pipeline_register_viewer_3_b_is_enabled,
       pipeline_register_viewer_3_c_is_enabled, pipeline_register_viewer_4_c_is_enabled, register_1_q,
       register_2_q, register_bank_viewer_1_a_is_enabled, register_bank_viewer_1_b_is_enabled,
       register_bank_viewer_1_c_is_enabled, uc1_1_p5, uc1_1_p6, UC1_HOLD, undriven, undriven_2, undriven_3,
       undriven_5, undriven_6;
  wire [1:0] MREtapa2Pipeline, MRMW, pipeline_register_1_mrymw_out, pipeline_register_1_sh_out, undriven_4;
  wire [3:0] pipeline_register_1_aluc_out, pipeline_register_viewer_1_b0, pipeline_register_viewer_1_b1,
       pipeline_register_viewer_1_b2, pipeline_register_viewer_1_b3, pipeline_register_viewer_1_b4,
       pipeline_register_viewer_1_b5, pipeline_register_viewer_1_b6, pipeline_register_viewer_1_b7,
       pipeline_register_viewer_1_b8, pipeline_register_viewer_1_b9, pipeline_register_viewer_1_b10,
       pipeline_register_viewer_1_b11, pipeline_register_viewer_1_b12, pipeline_register_viewer_1_b13,
       pipeline_register_viewer_1_b14, pipeline_register_viewer_1_b15, pipeline_register_viewer_1_b16,
       pipeline_register_viewer_1_c_lsn, pipeline_register_viewer_1_c_msn, pipeline_register_viewer_2_b0,
       pipeline_register_viewer_2_b1, pipeline_register_viewer_2_b2, pipeline_register_viewer_2_b3,
       pipeline_register_viewer_2_b4, pipeline_register_viewer_2_b5, pipeline_register_viewer_2_b6,
       pipeline_register_viewer_2_b7, pipeline_register_viewer_2_b8, pipeline_register_viewer_2_b9,
       pipeline_register_viewer_2_b10, pipeline_register_viewer_2_b11, pipeline_register_viewer_2_b12,
       pipeline_register_viewer_2_b13, pipeline_register_viewer_2_b14, pipeline_register_viewer_2_b15,
       pipeline_register_viewer_2_b16, pipeline_register_viewer_2_c_lsn, pipeline_register_viewer_2_c_msn,
       pipeline_register_viewer_3_a_lsn, pipeline_register_viewer_3_a_msn, pipeline_register_viewer_3_b0,
       pipeline_register_viewer_3_b1, pipeline_register_viewer_3_b2, pipeline_register_viewer_3_b3,
       pipeline_register_viewer_3_b4, pipeline_register_viewer_3_b5, pipeline_register_viewer_3_b6,
       pipeline_register_viewer_3_b7, pipeline_register_viewer_3_b8, pipeline_register_viewer_3_b9,
       pipeline_register_viewer_3_b10, pipeline_register_viewer_3_b11, pipeline_register_viewer_3_b12,
       pipeline_register_viewer_3_b13, pipeline_register_viewer_3_b14, pipeline_register_viewer_3_b15,
       pipeline_register_viewer_3_b16, pipeline_register_viewer_3_b_lsn, pipeline_register_viewer_3_b_msn,
       pipeline_register_viewer_3_c_lsn, pipeline_register_viewer_3_c_msn, pipeline_register_viewer_4_b0,
       pipeline_register_viewer_4_b1, pipeline_register_viewer_4_b2, pipeline_register_viewer_4_b3,
       pipeline_register_viewer_4_b4, pipeline_register_viewer_4_b5, pipeline_register_viewer_4_b6,
       pipeline_register_viewer_4_b7, pipeline_register_viewer_4_b8, pipeline_register_viewer_4_b9,
       pipeline_register_viewer_4_b10, pipeline_register_viewer_4_b11, pipeline_register_viewer_4_b12,
       pipeline_register_viewer_4_b13, pipeline_register_viewer_4_b14, pipeline_register_viewer_4_b15,
       pipeline_register_viewer_4_b16, pipeline_register_viewer_4_c_lsn, pipeline_register_viewer_4_c_msn,
       register_bank_viewer_1_a_address_n0, register_bank_viewer_1_a_address_n1,
       register_bank_viewer_1_a_address_n2, register_bank_viewer_1_a_address_n3,
       register_bank_viewer_1_a_data_lsn, register_bank_viewer_1_a_data_msn,
       register_bank_viewer_1_b_address_n0, register_bank_viewer_1_b_address_n1,
       register_bank_viewer_1_b_address_n2, register_bank_viewer_1_b_address_n3,
       register_bank_viewer_1_b_data_lsn, register_bank_viewer_1_b_data_msn,
       register_bank_viewer_1_c_address_n0, register_bank_viewer_1_c_address_n1,
       register_bank_viewer_1_c_address_n2, register_bank_viewer_1_c_address_n3,
       register_bank_viewer_1_c_data_lsn, register_bank_viewer_1_c_data_msn;
  wire [5:0] A_Etapa1, ALU_Pipeline_a_bus_out, ALU_Pipeline_b_bus_out, ALU_Pipeline_c_bus_out, B_Etapa1,
       C_Etapa1, C_Etapa2Alu, C_Etapa3, judge_1_a_bus, judge_1_b_bus, LoadStore_a_bus_out,
       LoadStore_b_bus_out, LoadStore_c_bus_out, pipeline_register_1_a_bus_out,
       pipeline_register_1_b_bus_out, pipeline_register_1_t_bus_out, pipeline_register_2_a_bus_out,
       pipeline_register_2_b_bus_out, reg_C_address;
  wire [8:8] pipeline_register_1_kmx_out;
  wire [9:0] ALU_Pipeline_d_address_out, instruction2register_1_daddresss, LoadStore_d_address_out,
       pipeline_register_1_d_address_out, register_3_q;
  wire [10:0] ProgramCounterReg_pc;
  wire [14:0] ALU_Pipeline_t_bus_out, judge_1_reg_out, LoadStore_t_bus_out,
       MicroInstructionROM_microinstruction, pipeline_register_2_t_bus_out;
  wire [15:0] ALU_RESULT, ALUALULAU_z, BusA_ALU_q, BusA_LS_q, BusB_ALU_q, Constant_K_q, data_1_datamemout,
       instruction2register_1_k, multiplexer_1_out, reg_A_read, reg_B_read, reg_C_write, register_6_q;
  wire [23:0] BBUS, ProgramMemory_data;

  DipSwitch #(.number(2)) dipswitch_1 (.sw1(dipswitch_1_sw1));  // open: sw2
  // Probe on ProgramCounterReg_pc
  ROM #(.addrWidth(11), .dataWidth(24)) ProgramMemory (.addr(ProgramCounterReg_pc), .data(ProgramMemory_data));
  // Probe on undriven
  // Probe on undriven_2
  // Probe on undriven_3
  // Probe on undriven_4[1]
  // Probe on undriven_4[0]
  // Probe on undriven_5
  and and_1 (and_1_out, BBUS[22], bloque1_1_preload);
  Bloque1 bloque1_1 (.Preload(bloque1_1_preload), .jump_type(BBUS[21:20]), .CY(CYin), .register_to_test(16'hfff));
  or or_1 (or_1_out, HOLD, UC1_HOLD);
  ClockGenerator clocks (.Auto(dipswitch_1_sw1), .ManualCLK(in_1), .CLK(CLK), .CLK2(CLK2), .CLK3(CLK3), .CLK4(CLK4));
  not not_1 (not_1_out, or_2_out);
  Register #(.width(24)) InstructionRegister (
    .D(ProgramMemory_data), .en(not_1_out), .clk(CLK), .Q(BBUS));  // open: clr
  or or_2 (or_2_out, HOLD, UC1_HOLD);
  PCreg ProgramCounterReg (
    .PC(ProgramCounterReg_pc), .displacement_or_address(BBUS[15:5]), .HOLD(or_1_out), .CLK1(CLK),
    .Preload(and_1_out));
  // Probe on BBUS
  Hex_Digit_Display hex_digit_display_1 (.value(register_bank_viewer_1_c_data_msn));  // open: dp
  Hex_Digit_Display hex_digit_display_2 (.value(register_bank_viewer_1_c_data_lsn));  // open: dp
  LED led_1 (.in(register_bank_viewer_1_c_is_enabled));
  Hex_Digit_Display hex_digit_display_3 (.value(register_bank_viewer_1_c_address_n3));  // open: dp
  Hex_Digit_Display hex_digit_display_4 (.value(register_bank_viewer_1_c_address_n2));  // open: dp
  Hex_Digit_Display hex_digit_display_5 (.value(register_bank_viewer_1_c_address_n1));  // open: dp
  Hex_Digit_Display hex_digit_display_6 (.value(register_bank_viewer_1_c_address_n0));  // open: dp
  Hex_Digit_Display hex_digit_display_7 (.value(register_bank_viewer_1_a_data_msn));  // open: dp
  Hex_Digit_Display hex_digit_display_8 (.value(register_bank_viewer_1_a_data_lsn));  // open: dp
  instruction2register instruction2register_1 (
    .Instruction(BBUS), .Daddresss(instruction2register_1_daddresss), .A(A_Etapa1), .B(B_Etapa1),
    .C(C_Etapa1), .K(instruction2register_1_k));
  or or_3 (or_3_out, HOLD, UC1_HOLD);
  Hex_Digit_Display hex_digit_display_9 (.value(register_bank_viewer_1_a_address_n3));  // open: dp
  Hex_Digit_Display hex_digit_display_10 (.value(register_bank_viewer_1_a_address_n2));  // open: dp
  Micro_Instruction_ROM MicroInstructionROM (
    .Instruction(BBUS), .MicroInstruction(MicroInstructionROM_microinstruction));
  LED led_2 (.in(register_bank_viewer_1_a_is_enabled));
  register_bank_viewer register_bank_viewer_1 (
    .B_data_MSN(register_bank_viewer_1_b_data_msn), .C_is_enabled(register_bank_viewer_1_c_is_enabled),
    .B_is_enabled(register_bank_viewer_1_b_is_enabled), .A_data_MSN(register_bank_viewer_1_a_data_msn),
    .C_address_N3(register_bank_viewer_1_c_address_n3), .A_data_LSN(register_bank_viewer_1_a_data_lsn),
    .A_address_N0(register_bank_viewer_1_a_address_n0), .C_address_N1(register_bank_viewer_1_c_address_n1),
    .B_address(reg_B_read), .B_address_N2(register_bank_viewer_1_b_address_n2), .A_address(reg_A_read),
    .C_address_N0(register_bank_viewer_1_c_address_n0), .A_address_N2(register_bank_viewer_1_a_address_n2),
    .B_address_N1(register_bank_viewer_1_b_address_n1), .B_data_out(pipeline_register_1_b_bus_out),
    .C_data_LSN(register_bank_viewer_1_c_data_lsn), .A_address_N3(register_bank_viewer_1_a_address_n3),
    .A_address_N1(register_bank_viewer_1_a_address_n1), .C_data_MSN(register_bank_viewer_1_c_data_msn),
    .C_data_out(reg_C_address), .B_address_N3(register_bank_viewer_1_b_address_n3),
    .A_data_out(pipeline_register_1_a_bus_out), .B_address_N0(register_bank_viewer_1_b_address_n0),
    .B_data_LSN(register_bank_viewer_1_b_data_lsn), .C_address(reg_C_write),
    .C_address_N2(register_bank_viewer_1_c_address_n2), .A_is_enabled(register_bank_viewer_1_a_is_enabled));
  Hex_Digit_Display hex_digit_display_11 (.value(register_bank_viewer_1_a_address_n0));  // open: dp
  Hex_Digit_Display hex_digit_display_12 (.value(register_bank_viewer_1_a_address_n1));  // open: dp
  DotMatrix #(.matrixcols(17), .matrixrows(4)) dotmatrix_1 (
    .col0(pipeline_register_viewer_1_b16), .col1(pipeline_register_viewer_1_b15),
    .col2(pipeline_register_viewer_1_b14), .col3(pipeline_register_viewer_1_b13),
    .col4(pipeline_register_viewer_1_b12), .col5(pipeline_register_viewer_1_b11),
    .col6(pipeline_register_viewer_1_b10), .col7(pipeline_register_viewer_1_b9),
    .col8(pipeline_register_viewer_1_b8), .col9(pipeline_register_viewer_1_b7),
    .col10(pipeline_register_viewer_1_b6), .col11(pipeline_register_viewer_1_b5),
    .col12(pipeline_register_viewer_1_b4), .col13(pipeline_register_viewer_1_b3),
    .col14(pipeline_register_viewer_1_b2), .col15(pipeline_register_viewer_1_b1),
    .col16(pipeline_register_viewer_1_b0));
  pipeline_register_viewer pipeline_register_viewer_1 (
    .b11(pipeline_register_viewer_1_b11), .b8(pipeline_register_viewer_1_b8),
    .microinstruction({pipeline_register_1_aluc_out, pipeline_register_1_sh_out, pipeline_register_1_kmx_out[8], pipeline_register_1_mrymw_out, pipeline_register_1_t_bus_out}),
    .b1(pipeline_register_viewer_1_b1), .B_in(pipeline_register_1_b_bus_out),
    .b10(pipeline_register_viewer_1_b10), .b9(pipeline_register_viewer_1_b9),
    .b0(pipeline_register_viewer_1_b0), .A_in(pipeline_register_1_a_bus_out),
    .b13(pipeline_register_viewer_1_b13), .b14(pipeline_register_viewer_1_b14),
    .b3(pipeline_register_viewer_1_b3), .b16(pipeline_register_viewer_1_b16),
    .b12(pipeline_register_viewer_1_b12), .b7(pipeline_register_viewer_1_b7),
    .b2(pipeline_register_viewer_1_b2), .C_in(C_Etapa2Alu), .b15(pipeline_register_viewer_1_b15),
    .b4(pipeline_register_viewer_1_b4), .b5(pipeline_register_viewer_1_b5),
    .b6(pipeline_register_viewer_1_b6), .C_is_enabled(pipeline_register_viewer_1_c_is_enabled),
    .C_MSN(pipeline_register_viewer_1_c_msn), .C_LSN(pipeline_register_viewer_1_c_lsn));  // open: A_is_enabled, A_MSN, B_MSN, A_LSN, B_is_enabled, B_LSN
  // Probe on MicroInstructionROM_microinstruction[14:11]
  // Probe on MicroInstructionROM_microinstruction[10:9]
  // Probe on MicroInstructionROM_microinstruction[8]
  // Probe on MicroInstructionROM_microinstruction[7]
  // Probe on MicroInstructionROM_microinstruction[6]
  // Probe on MicroInstructionROM_microinstruction[5:0]
  Hex_Digit_Display hex_digit_display_13 (.value(register_bank_viewer_1_b_data_lsn));  // open: dp
  Hex_Digit_Display hex_digit_display_14 (.value(register_bank_viewer_1_b_data_msn));  // open: dp
  Hex_Digit_Display hex_digit_display_15 (.value(register_bank_viewer_1_b_address_n3));  // open: dp
  Hex_Digit_Display hex_digit_display_16 (.value(register_bank_viewer_1_b_address_n2));  // open: dp
  Hex_Digit_Display hex_digit_display_17 (.value(pipeline_register_viewer_1_c_msn));  // open: dp
  LED led_3 (.in(register_bank_viewer_1_b_is_enabled));
  Hex_Digit_Display hex_digit_display_18 (.value(register_bank_viewer_1_b_address_n0));  // open: dp
  Hex_Digit_Display hex_digit_display_19 (.value(register_bank_viewer_1_b_address_n1));  // open: dp
  LED led_4 (.in(pipeline_register_viewer_1_c_is_enabled));
  Hex_Digit_Display hex_digit_display_20 (.value(pipeline_register_viewer_1_c_lsn));  // open: dp
  Pipeline_register pipeline_register_1 (
    .ALUC_OUT(pipeline_register_1_aluc_out), .B_bus_IN(B_Etapa1),
    .SH_IN(MicroInstructionROM_microinstruction[10:9]), .D_Address_OUT(pipeline_register_1_d_address_out),
    .C_bus_OUT(C_Etapa2Alu), .A_bus_OUT(pipeline_register_1_a_bus_out),
    .ALUC_IN(MicroInstructionROM_microinstruction[14:11]), .A_bus_IN(A_Etapa1),
    .D_Address_IN(instruction2register_1_daddresss), .MRyMW_OUT(pipeline_register_1_mrymw_out),
    .SH_OUT(pipeline_register_1_sh_out), .C_bus_IN(C_Etapa1),
    .Kmx_IN(MicroInstructionROM_microinstruction[8]), .Hold(or_3_out),
    .B_bus_OUT(pipeline_register_1_b_bus_out), .T_bus_OUT(pipeline_register_1_t_bus_out), .CLK(CLK2),
    .MRyMW_IN(MicroInstructionROM_microinstruction[7:6]),
    .T_bus_IN(MicroInstructionROM_microinstruction[5:0]), .Kmx_OUT(pipeline_register_1_kmx_out[8]));
  LED led_5 ();  // open: in
  Hex_Digit_Display hex_digit_display_21 ();  // open: value, dp
  Hex_Digit_Display hex_digit_display_22 ();  // open: value, dp
  // register_bank register_bank_1: pin names not known; wires that end beside it: reg_A_read, CLK, reg_B_read, reg_C_write, reg_C_address, pipeline_register_1_a_bus_out, pipeline_register_1_b_bus_out
  LED led_6 ();  // open: in
  Hex_Digit_Display hex_digit_display_23 ();  // open: value, dp
  Hex_Digit_Display hex_digit_display_24 ();  // open: value, dp
  // UC1 uc1_1: pin names not known; wires that end beside it: mem_is_free, HOLD, pipeline_register_1_mrymw_out, ALU_is_free, uc1_1_p5, uc1_1_p6, UC1_HOLD
  Register #(.width(1)) register_1 (.D(uc1_1_p5), .clk(CLK2), .Q(register_1_q));  // open: en, clr
  Register #(.width(16), .trigger("falling")) Constant_K (
    .D(instruction2register_1_k), .clk(CLK2), .Q(Constant_K_q));  // open: en, clr
  Register #(.width(1), .trigger("falling")) register_2 (.D(uc1_1_p6), .clk(CLK2), .Q(register_2_q));  // open: en, clr
  not not_2 (not_2_out, pipeline_register_1_kmx_out[8]);
  Register #(.width(16)) BusA_ALU (.D(multiplexer_1_out), .en(uc1_1_p5), .clk(CLK2), .Q(BusA_ALU_q));  // open: clr
  Multiplexer #(.width(16), .enable("false")) multiplexer_1 (
    .in0(Constant_K_q), .in1(reg_A_read), .out(multiplexer_1_out), .sel(not_2_out));
  Register #(.width(16)) BusB_ALU (.D(reg_B_read), .en(uc1_1_p5), .clk(CLK2), .Q(BusB_ALU_q));  // open: clr
  Register #(.width(10)) register_3 (
    .D(pipeline_register_1_d_address_out), .en(uc1_1_p6), .clk(CLK2), .Q(register_3_q));  // open: clr
  DotMatrix #(.matrixcols(17), .matrixrows(4)) dotmatrix_2 (
    .col0(pipeline_register_viewer_2_b16), .col1(pipeline_register_viewer_2_b15),
    .col2(pipeline_register_viewer_2_b14), .col3(pipeline_register_viewer_2_b13),
    .col4(pipeline_register_viewer_2_b12), .col5(pipeline_register_viewer_2_b11),
    .col6(pipeline_register_viewer_2_b10), .col7(pipeline_register_viewer_2_b9),
    .col8(pipeline_register_viewer_2_b8), .col9(pipeline_register_viewer_2_b7),
    .col10(pipeline_register_viewer_2_b6), .col11(pipeline_register_viewer_2_b5),
    .col12(pipeline_register_viewer_2_b4), .col13(pipeline_register_viewer_2_b3),
    .col14(pipeline_register_viewer_2_b2), .col15(pipeline_register_viewer_2_b1),
    .col16(pipeline_register_viewer_2_b0));
  pipeline_register_viewer pipeline_register_viewer_2 (
    .b11(pipeline_register_viewer_2_b11), .b8(pipeline_register_viewer_2_b8),
    .microinstruction({ALU_Pipeline_t_bus_out[14:8], MREtapa2Pipeline, ALU_Pipeline_t_bus_out[5:0]}),
    .b1(pipeline_register_viewer_2_b1), .B_in(ALU_Pipeline_b_bus_out), .b10(pipeline_register_viewer_2_b10),
    .b9(pipeline_register_viewer_2_b9), .b0(pipeline_register_viewer_2_b0), .A_in(ALU_Pipeline_a_bus_out),
    .b13(pipeline_register_viewer_2_b13), .b14(pipeline_register_viewer_2_b14),
    .b3(pipeline_register_viewer_2_b3), .b16(pipeline_register_viewer_2_b16),
    .b12(pipeline_register_viewer_2_b12), .b7(pipeline_register_viewer_2_b7),
    .b2(pipeline_register_viewer_2_b2), .C_in(ALU_Pipeline_c_bus_out), .b15(pipeline_register_viewer_2_b15),
    .b4(pipeline_register_viewer_2_b4), .b5(pipeline_register_viewer_2_b5),
    .b6(pipeline_register_viewer_2_b6), .C_is_enabled(pipeline_register_viewer_2_c_is_enabled),
    .C_MSN(pipeline_register_viewer_2_c_msn), .C_LSN(pipeline_register_viewer_2_c_lsn));  // open: A_is_enabled, A_MSN, B_MSN, A_LSN, B_is_enabled, B_LSN
  not not_3 (not_3_out, uc1_1_p5);
  and and_2 (and_2_out, register_1_q, CLK3);
  and and_3 (and_3_out, ~CLK3, register_2_q);  // AND_Gate
  Register #(.width(16)) BusA_LS (.D(reg_A_read), .en(uc1_1_p6), .clk(CLK2), .Q(BusA_LS_q));  // open: clr
  // Probe on BusA_ALU_q
  // Probe on BusB_ALU_q
  DotMatrix #(.matrixcols(17), .matrixrows(4)) dotmatrix_3 (
    .col0(pipeline_register_viewer_3_b16), .col1(pipeline_register_viewer_3_b15),
    .col2(pipeline_register_viewer_3_b14), .col3(pipeline_register_viewer_3_b13),
    .col4(pipeline_register_viewer_3_b12), .col5(pipeline_register_viewer_3_b11),
    .col6(pipeline_register_viewer_3_b10), .col7(pipeline_register_viewer_3_b9),
    .col8(pipeline_register_viewer_3_b8), .col9(pipeline_register_viewer_3_b7),
    .col10(pipeline_register_viewer_3_b6), .col11(pipeline_register_viewer_3_b5),
    .col12(pipeline_register_viewer_3_b4), .col13(pipeline_register_viewer_3_b3),
    .col14(pipeline_register_viewer_3_b2), .col15(pipeline_register_viewer_3_b1),
    .col16(pipeline_register_viewer_3_b0));
  pipeline_register_viewer pipeline_register_viewer_3 (
    .A_is_enabled(pipeline_register_viewer_3_a_is_enabled), .b11(pipeline_register_viewer_3_b11),
    .b8(pipeline_register_viewer_3_b8),
    .microinstruction({LoadStore_t_bus_out[14:8], MRMW, LoadStore_t_bus_out[5:0]}),
    .b1(pipeline_register_viewer_3_b1), .B_in(LoadStore_b_bus_out), .b10(pipeline_register_viewer_3_b10),
    .b9(pipeline_register_viewer_3_b9), .A_MSN(pipeline_register_viewer_3_a_msn),
    .b0(pipeline_register_viewer_3_b0), .A_in(LoadStore_a_bus_out), .b13(pipeline_register_viewer_3_b13),
    .b14(pipeline_register_viewer_3_b14), .B_MSN(pipeline_register_viewer_3_b_msn),
    .b3(pipeline_register_viewer_3_b3), .b16(pipeline_register_viewer_3_b16),
    .b12(pipeline_register_viewer_3_b12), .b7(pipeline_register_viewer_3_b7),
    .A_LSN(pipeline_register_viewer_3_a_lsn), .b2(pipeline_register_viewer_3_b2), .C_in(LoadStore_c_bus_out),
    .b15(pipeline_register_viewer_3_b15), .b4(pipeline_register_viewer_3_b4),
    .B_is_enabled(pipeline_register_viewer_3_b_is_enabled), .b5(pipeline_register_viewer_3_b5),
    .b6(pipeline_register_viewer_3_b6), .B_LSN(pipeline_register_viewer_3_b_lsn),
    .C_is_enabled(pipeline_register_viewer_3_c_is_enabled), .C_MSN(pipeline_register_viewer_3_c_msn),
    .C_LSN(pipeline_register_viewer_3_c_lsn));
  not not_4 (not_4_out, uc1_1_p6);
  and and_4 (and_4_out, ALU_is_done, ~ALU_is_free);  // AND_Gate
  Register #(.width(1)) register_4 (.D(ALUALULAU_cyout), .en(1'b1), .clk(CLK2), .Q(CYin));  // open: clr
  LED led_7 (.in(pipeline_register_viewer_2_c_is_enabled));
  Hex_Digit_Display hex_digit_display_25 (.value(pipeline_register_viewer_2_c_msn));  // open: dp
  ALU ALUALULAU (
    .ALUC(ALU_Pipeline_t_bus_out[14:11]), .A(BusA_ALU_q), .B(BusB_ALU_q), .CYin(CYin), .Z(ALUALULAU_z),
    .CYout(ALUALULAU_cyout));
  Hex_Digit_Display hex_digit_display_26 (.value(pipeline_register_viewer_2_c_lsn));  // open: dp
  Hex_Digit_Display hex_digit_display_27 ();  // open: value, dp
  Pipeline_register ALU_Pipeline (
    .ALUC_OUT(ALU_Pipeline_t_bus_out[14:11]), .B_bus_IN(pipeline_register_1_b_bus_out),
    .SH_IN(pipeline_register_1_sh_out), .D_Address_OUT(ALU_Pipeline_d_address_out),
    .C_bus_OUT(ALU_Pipeline_c_bus_out), .A_bus_OUT(ALU_Pipeline_a_bus_out),
    .ALUC_IN(pipeline_register_1_aluc_out), .A_bus_IN(pipeline_register_1_a_bus_out),
    .D_Address_IN(pipeline_register_1_d_address_out), .MRyMW_OUT(MREtapa2Pipeline),
    .SH_OUT(ALU_Pipeline_t_bus_out[10:9]), .C_bus_IN(C_Etapa2Alu), .Kmx_IN(pipeline_register_1_kmx_out[8]),
    .Hold(not_3_out), .B_bus_OUT(ALU_Pipeline_b_bus_out), .T_bus_OUT(ALU_Pipeline_t_bus_out[5:0]),
    .CLK(CLK3), .MRyMW_IN(pipeline_register_1_mrymw_out), .T_bus_IN(pipeline_register_1_t_bus_out),
    .Kmx_OUT(ALU_Pipeline_t_bus_out[8]));
  ALU_unit_control alu_unit_control_1 (
    .set_free(and_4_out), .set_not_free(and_2_out), .clk(CLK3), .is_free(ALU_is_free), .is_done(ALU_is_done));
  // Probe on ALUALULAU_z
  LED led_8 (.in(pipeline_register_viewer_3_c_is_enabled));
  Hex_Digit_Display hex_digit_display_28 (.value(pipeline_register_viewer_3_c_lsn));  // open: dp
  Hex_Digit_Display hex_digit_display_29 (.value(pipeline_register_viewer_3_c_msn));  // open: dp
  Pipeline_register LoadStore (
    .ALUC_OUT(LoadStore_t_bus_out[14:11]), .B_bus_IN(pipeline_register_1_b_bus_out),
    .SH_IN(pipeline_register_1_sh_out), .D_Address_OUT(LoadStore_d_address_out),
    .C_bus_OUT(LoadStore_c_bus_out), .A_bus_OUT(LoadStore_a_bus_out), .ALUC_IN(pipeline_register_1_aluc_out),
    .A_bus_IN(pipeline_register_1_a_bus_out), .D_Address_IN(pipeline_register_1_d_address_out),
    .MRyMW_OUT(MRMW), .SH_OUT(LoadStore_t_bus_out[10:9]), .C_bus_IN(C_Etapa2Alu),
    .Kmx_IN(pipeline_register_1_kmx_out[8]), .Hold(not_4_out), .B_bus_OUT(LoadStore_b_bus_out),
    .T_bus_OUT(LoadStore_t_bus_out[5:0]), .CLK(CLK3), .MRyMW_IN(pipeline_register_1_mrymw_out),
    .T_bus_IN(pipeline_register_1_t_bus_out), .Kmx_OUT(LoadStore_t_bus_out[8]));
  LED led_9 ();  // open: in
  Hex_Digit_Display hex_digit_display_30 ();  // open: value, dp
  Register #(.width(16)) register_5 (.D(ALUALULAU_z), .en(1'b1), .clk(CLK2), .Q(ALU_RESULT));  // open: clr
  LED led_10 (.in(pipeline_register_viewer_3_a_is_enabled));
  Hex_Digit_Display hex_digit_display_31 (.value(pipeline_register_viewer_3_a_msn));  // open: dp
  Hex_Digit_Display hex_digit_display_32 (.value(pipeline_register_viewer_3_a_lsn));  // open: dp
  and and_5 (and_5_out, MEM_is_done, ~mem_is_free);  // AND_Gate
  Data data_1 (
    .DAddress(register_3_q), .M(MRMW), .clk(CLK2), .Enable(register_2_q), .DataMemInput(BusA_LS_q),
    .DataMemOut(data_1_datamemout));
  LED led_11 ();  // open: in
  Hex_Digit_Display hex_digit_display_33 ();  // open: value, dp
  Hex_Digit_Display hex_digit_display_34 ();  // open: value, dp
  LED led_12 (.in(pipeline_register_viewer_3_b_is_enabled));
  Hex_Digit_Display hex_digit_display_35 (.value(pipeline_register_viewer_3_b_msn));  // open: dp
  // Probe on MRMW
  // Probe on LoadStore_d_address_out
  // Probe on data_1_datamemout
  Hex_Digit_Display hex_digit_display_36 (.value(pipeline_register_viewer_3_b_lsn));  // open: dp
  memory_unit_control memory_unit_control_1 (
    .set_free(and_5_out), .set_not_free(and_3_out), .clk(CLK2), .is_free(mem_is_free), .is_done(MEM_is_done));
  // Probe on mem_is_free
  Register #(.width(16)) register_6 (.D(data_1_datamemout), .en(1'b1), .clk(CLK2), .Q(register_6_q));  // open: clr
  Multiplexer #(.width(16), .enable("false")) multiplexer_2 (
    .in0(ALU_RESULT), .in1(register_6_q), .out(reg_C_write), .sel(MEM_is_done));
  judge judge_1 (
    .reg_in_alu({ALU_Pipeline_t_bus_out[14:8], MREtapa2Pipeline, ALU_Pipeline_t_bus_out[5:0]}),
    .reg_in_memory({LoadStore_t_bus_out[14:8], MRMW, LoadStore_t_bus_out[5:0]}),
    .A_alu(ALU_Pipeline_a_bus_out), .A_mem(LoadStore_a_bus_out), .B_alu(ALU_Pipeline_b_bus_out),
    .B_mem(LoadStore_b_bus_out), .C_alu(ALU_Pipeline_c_bus_out), .C_mem(LoadStore_c_bus_out),
    .in_9({MEM_is_done, ALU_is_done}), .reg_out(judge_1_reg_out), .A_bus(judge_1_a_bus),
    .B_bus(judge_1_b_bus), .C_bus(C_Etapa3));
  UC2 uc2_1 (
    .A_etapa_1(A_Etapa1), .B_etapa_1(B_Etapa1), .C_etapa_1(C_Etapa1), .C_etapa_2_ALU(C_Etapa2Alu),
    .ALU_is_done(ALU_is_free), .C_etapa_2_MEM(C_Etapa2Alu), .MEM_is_done(mem_is_free), .C_etapa_3(C_Etapa3),
    .clk(CLK), .out_10(HOLD));
  DotMatrix #(.matrixcols(17), .matrixrows(4)) dotmatrix_4 (
    .col0(pipeline_register_viewer_4_b16), .col1(pipeline_register_viewer_4_b15),
    .col2(pipeline_register_viewer_4_b14), .col3(pipeline_register_viewer_4_b13),
    .col4(pipeline_register_viewer_4_b12), .col5(pipeline_register_viewer_4_b11),
    .col6(pipeline_register_viewer_4_b10), .col7(pipeline_register_viewer_4_b9),
    .col8(pipeline_register_viewer_4_b8), .col9(pipeline_register_viewer_4_b7),
    .col10(pipeline_register_viewer_4_b6), .col11(pipeline_register_viewer_4_b5),
    .col12(pipeline_register_viewer_4_b4), .col13(pipeline_register_viewer_4_b3),
    .col14(pipeline_register_viewer_4_b2), .col15(pipeline_register_viewer_4_b1),
    .col16(pipeline_register_viewer_4_b0));
  pipeline_register_viewer pipeline_register_viewer_4 (
    .b11(pipeline_register_viewer_4_b11), .b8(pipeline_register_viewer_4_b8),
    .microinstruction(pipeline_register_2_t_bus_out), .b1(pipeline_register_viewer_4_b1),
    .B_in(pipeline_register_2_b_bus_out), .b10(pipeline_register_viewer_4_b10),
    .b9(pipeline_register_viewer_4_b9), .b0(pipeline_register_viewer_4_b0),
    .A_in(pipeline_register_2_a_bus_out), .b13(pipeline_register_viewer_4_b13),
    .b14(pipeline_register_viewer_4_b14), .b3(pipeline_register_viewer_4_b3),
    .b16(pipeline_register_viewer_4_b16), .b12(pipeline_register_viewer_4_b12),
    .b7(pipeline_register_viewer_4_b7), .b2(pipeline_register_viewer_4_b2), .C_in(reg_C_address),
    .b15(pipeline_register_viewer_4_b15), .b4(pipeline_register_viewer_4_b4),
    .b5(pipeline_register_viewer_4_b5), .b6(pipeline_register_viewer_4_b6),
    .C_is_enabled(pipeline_register_viewer_4_c_is_enabled), .C_MSN(pipeline_register_viewer_4_c_msn),
    .C_LSN(pipeline_register_viewer_4_c_lsn));  // open: A_is_enabled, A_MSN, B_MSN, A_LSN, B_is_enabled, B_LSN
  LED led_13 (.in(pipeline_register_viewer_4_c_is_enabled));
  Hex_Digit_Display hex_digit_display_37 (.value(pipeline_register_viewer_4_c_lsn));  // open: dp
  Hex_Digit_Display hex_digit_display_38 (.value(pipeline_register_viewer_4_c_msn));  // open: dp
  Pipeline_register pipeline_register_2 (
    .ALUC_OUT(pipeline_register_2_t_bus_out[14:11]), .B_bus_IN(judge_1_b_bus), .SH_IN(judge_1_reg_out[10:9]),
    .C_bus_OUT(reg_C_address), .A_bus_OUT(pipeline_register_2_a_bus_out), .ALUC_IN(judge_1_reg_out[14:11]),
    .A_bus_IN(judge_1_a_bus), .MRyMW_OUT(pipeline_register_2_t_bus_out[7:6]),
    .SH_OUT(pipeline_register_2_t_bus_out[10:9]), .C_bus_IN(C_Etapa3), .Kmx_IN(judge_1_reg_out[8]),
    .Hold(undriven_6), .B_bus_OUT(pipeline_register_2_b_bus_out),
    .T_bus_OUT(pipeline_register_2_t_bus_out[5:0]), .CLK(CLK3), .MRyMW_IN(judge_1_reg_out[7:6]),
    .T_bus_IN(judge_1_reg_out[5:0]), .Kmx_OUT(pipeline_register_2_t_bus_out[8]));  // open: D_Address_OUT, D_Address_IN
  LED led_14 ();  // open: in
  Hex_Digit_Display hex_digit_display_39 ();  // open: value, dp
  Hex_Digit_Display hex_digit_display_40 ();  // open: value, dp
  LED led_15 ();  // open: in
  Hex_Digit_Display hex_digit_display_41 ();  // open: value, dp
  Hex_Digit_Display hex_digit_display_42 ();  // open: value, dp
  // NOT_Gate not_5 is placed but not wired

  // Other names for the same wires on the sheet: C_Etapa2Mem[5:0] = C_Etapa2Alu; pulseGenManual = in_1

  // Notes on the sheet:
  //   contents of ProgramMemory (hex, n*v repeats v):
  //   300061 3000a2
  //   splitters que encajar con los registros de pipeline
  //   para hacer copy-paste
  //   probes que encajar en los splitters de arriba
  //   INSTRUCTION
  //   REGISTER
  //   Detecto nueva operacion de memoria
  //   El mux es el de los is_done , el menos significativo es el de la ALU que se pone en 1 cuando termino
endmodule
